// Logisim project 07-Encoder83.circ as structural Verilog: 1 circuit, main circuit main
module main (
  input  in_1,
  input  in_2,
  input  in_3,
  input  in_4,
  input  in_5,
  input  in_6,
  input  in_7,
  input  in_8,
  input  in_9,
  output out_10,
  output out_11,
  output out_12,
  output out_13
);

  or or_1 (out_10, in_1, in_3, in_5, in_7, in_9);
  or or_2 (out_11, in_3, in_2, in_6, in_7);
  or or_3 (out_12, in_4, in_5, in_6, in_7);
  or or_4 (out_13, in_8, in_9);
endmodule
